# Fritzing sketch schema (saved by Fritzing 0.9.2b)
breadboards: 1

parts:
  U1 = ESP8266 WiFi Module [part_number=ESP8266]
  Composant1 = Logic Level Converter
  Composant2 = FTDI Basic Programmer

nets:
  N1: U1.RXD, Composant1.RX_LV
  N2: U1.VCC, U1.CH_PD, Composant1.LV
  GND: U1.GPIO_0, U1.GND, Composant1.GND, Composant2.GND
  N3: U1.TXD, Composant1.TX_LV
  N4: Composant1.TX_HV, Composant2.RXI
  N5: Composant1.RX_HV, Composant2.TXO
  N6: Composant1.HV, Composant2.POWER

notes:
  Ce fil bleu n'est là que pour la procédure de flash
  3.3v

custom parts:
  ESP8266 WiFi Module: Generic WiFi Module based on the ESP8266 with onboard PCB antenna and UART communications

// code stored in the sketch: Sch├⌐ma 1.ino


// code stored in the sketch: SchΓö£╨╣ma 1.ino

